# Fritzing sketch schematic (saved by Fritzing 0.9.2b)
breadboards: 1

parts:
  U1 = PIC16F874A/877A [package=dil40]
  S1 = Momentary Switch [package=ksa_sealed_tac_switch]
  S2 = Round Pushbutton
  S3 = Momentary Switch [package=ksa_sealed_tac_switch]
  R1 = Resistor [tolerance=±5% resistance=22 package="2010 [SMD]"]
  T1 = LM35 Temperature Sensor [package="TO92 [THT]"]
  Q1 = MOSFET-NCHANNEL [package=to-92]
  V1 = DC Power [voltage=5V]
  V2 = DC Power [voltage=12V]
  FAN = DC Motor

nets:
  N1: U1.RA0/AN0, T1.Vout
  N2: U1.RE0/RD/AN5, Q1.G
  N3: U1.RD3/PSP3, S2.leg1
  N4: U1.RD4/PSP4, S3.4
  N5: U1.RD5/PSP5, S1.4
  VSS: U1.VSS, T1.GND, V1.V-
  N6: U1.VDD, S1.1, S2.leg0, S3.1, T1.+Vs, V1.V+
  N7: R1.Pin_0, V2.V-, FAN.pin_2
  N8: R1.Pin_1, Q1.D
  N9: Q1.S, V2.V+, FAN.pin_1

custom parts:
  PIC16F874A/877A: Microchip 6-bit
